// Logisim project RAM(4X3).circ as structural Verilog: 2 circuits, main circuit main
module main (
  input  [2:0] in_1,
  input  [1:0] in_2,
  input  WRITE_READ,
  output [2:0] out_4
);

  wire binary_cell_1_out_4, binary_cell_2_out_4, binary_cell_3_out_4, binary_cell_4_out_4,
       binary_cell_5_out_4, binary_cell_6_out_4, binary_cell_7_out_4, binary_cell_8_out_4,
       binary_cell_9_out_4, binary_cell_10_out_4, binary_cell_11_out_4, binary_cell_12_out_4, decoder_1_out0,
       decoder_1_out1, decoder_1_out2, decoder_1_out3;

  Decoder #(.select(2)) decoder_1 (
    .out0(decoder_1_out0), .out1(decoder_1_out1), .out2(decoder_1_out2), .out3(decoder_1_out3), .sel(in_2));  // open: en
  Binary_Cell binary_cell_1 (.in_1(decoder_1_out0), .in_2(in_1[0]), .in_3(WRITE_READ), .out_4(binary_cell_1_out_4));
  Binary_Cell binary_cell_2 (.in_1(decoder_1_out1), .in_2(in_1[0]), .in_3(WRITE_READ), .out_4(binary_cell_2_out_4));
  Binary_Cell binary_cell_3 (.in_1(decoder_1_out2), .in_2(in_1[0]), .in_3(WRITE_READ), .out_4(binary_cell_3_out_4));
  Binary_Cell binary_cell_4 (.in_1(decoder_1_out3), .in_2(in_1[0]), .in_3(WRITE_READ), .out_4(binary_cell_4_out_4));
  or or_1 (out_4[0], binary_cell_4_out_4, binary_cell_3_out_4, binary_cell_2_out_4, binary_cell_1_out_4);
  Binary_Cell binary_cell_5 (.in_1(decoder_1_out0), .in_2(in_1[1]), .in_3(WRITE_READ), .out_4(binary_cell_5_out_4));
  Binary_Cell binary_cell_6 (.in_1(decoder_1_out1), .in_2(in_1[1]), .in_3(WRITE_READ), .out_4(binary_cell_6_out_4));
  Binary_Cell binary_cell_7 (.in_1(decoder_1_out2), .in_2(in_1[1]), .in_3(WRITE_READ), .out_4(binary_cell_7_out_4));
  Binary_Cell binary_cell_8 (.in_1(decoder_1_out3), .in_2(in_1[1]), .in_3(WRITE_READ), .out_4(binary_cell_8_out_4));
  or or_2 (out_4[1], binary_cell_8_out_4, binary_cell_7_out_4, binary_cell_6_out_4, binary_cell_5_out_4);
  Binary_Cell binary_cell_9 (.in_1(decoder_1_out0), .in_2(in_1[2]), .in_3(WRITE_READ), .out_4(binary_cell_9_out_4));
  Binary_Cell binary_cell_10 (.in_1(decoder_1_out1), .in_2(in_1[2]), .in_3(WRITE_READ), .out_4(binary_cell_10_out_4));
  Binary_Cell binary_cell_11 (.in_1(decoder_1_out2), .in_2(in_1[2]), .in_3(WRITE_READ), .out_4(binary_cell_11_out_4));
  Binary_Cell binary_cell_12 (.in_1(decoder_1_out3), .in_2(in_1[2]), .in_3(WRITE_READ), .out_4(binary_cell_12_out_4));
  or or_3 (out_4[2], binary_cell_12_out_4, binary_cell_11_out_4, binary_cell_10_out_4, binary_cell_9_out_4);
endmodule

module Binary_Cell (
  input  in_1,
  input  in_2,
  input  in_3,
  output out_4
);

  wire and_1_out, and_2_out, clock_1_out, not_1_out, not_2_out, s_r_ff_1_q;

  Clock clock_1 (.out(clock_1_out));
  and and_1 (and_1_out, in_1, in_2, not_2_out);
  not not_1 (not_1_out, in_2);
  and and_2 (and_2_out, in_1, not_1_out, not_2_out);
  not not_2 (not_2_out, in_3);
  S_R_Flip_Flop s_r_ff_1 (
    .S(and_1_out), .clk(clock_1_out), .R(and_2_out), .Q(s_r_ff_1_q));  // open: Qn, preset, reset, en
  and and_3 (out_4, s_r_ff_1_q, in_1, in_3);
endmodule
