// Logisim project REGISTER TRANSFER LOGIC.circ as structural Verilog: 1 circuit, main circuit main
module main (
  input  [1:0] in_1,
  input  in_2,
  input  [1:0] in_3,
  input  RESET
);

  wire CLOCK_out, decoder_1_out0, decoder_1_out1, decoder_1_out2, decoder_1_out3;
  wire [7:0] multiplexer_1_out, register_1_q, register_2_q, register_3_q, register_4_q;

  Decoder #(.select(2)) decoder_1 (
    .out0(decoder_1_out0), .out1(decoder_1_out1), .out2(decoder_1_out2), .out3(decoder_1_out3), .sel(in_3),
    .en(in_2));
  Register register_1 (.D(multiplexer_1_out), .en(decoder_1_out0), .Q(register_1_q), .clk(CLOCK_out), .clr(RESET));
  Register register_2 (.D(multiplexer_1_out), .en(decoder_1_out1), .Q(register_2_q), .clk(CLOCK_out), .clr(RESET));
  Register register_3 (.D(multiplexer_1_out), .en(decoder_1_out2), .Q(register_3_q), .clk(CLOCK_out), .clr(RESET));
  Register register_4 (.D(multiplexer_1_out), .en(decoder_1_out3), .Q(register_4_q), .clk(CLOCK_out), .clr(RESET));
  Clock CLOCK (.out(CLOCK_out));
  Multiplexer #(.select(2)) multiplexer_1 (
    .in0(register_1_q[0]), .in1(register_2_q[0]), .in2(register_3_q[0]), .in3(register_4_q[0]),
    .out(multiplexer_1_out[0]), .sel(in_1), .en(in_2));
  Multiplexer #(.select(2)) multiplexer_2 (
    .in0(register_1_q[1]), .in1(register_2_q[1]), .in2(register_3_q[1]), .in3(register_4_q[1]),
    .out(multiplexer_1_out[1]), .sel(in_1), .en(in_2));
  Multiplexer #(.select(2)) multiplexer_3 (
    .in0(register_1_q[2]), .in1(register_2_q[2]), .in2(register_3_q[2]), .in3(register_4_q[2]),
    .out(multiplexer_1_out[2]), .sel(in_1), .en(in_2));
  Multiplexer #(.select(2)) multiplexer_4 (
    .in0(register_1_q[3]), .in1(register_2_q[3]), .in2(register_3_q[3]), .in3(register_4_q[3]),
    .out(multiplexer_1_out[3]), .sel(in_1), .en(in_2));
  Multiplexer #(.select(2)) multiplexer_5 (
    .in0(register_1_q[4]), .in1(register_2_q[4]), .in2(register_3_q[4]), .in3(register_4_q[4]),
    .out(multiplexer_1_out[4]), .sel(in_1), .en(in_2));
  Multiplexer #(.select(2)) multiplexer_6 (
    .in0(register_1_q[5]), .in1(register_2_q[5]), .in2(register_3_q[5]), .in3(register_4_q[5]),
    .out(multiplexer_1_out[5]), .sel(in_1), .en(in_2));
  Multiplexer #(.select(2)) multiplexer_7 (
    .in0(register_1_q[6]), .in1(register_2_q[6]), .in2(register_3_q[6]), .in3(register_4_q[6]),
    .out(multiplexer_1_out[6]), .sel(in_1), .en(in_2));
  Multiplexer #(.select(2)) multiplexer_8 (
    .in0(register_1_q[7]), .in1(register_2_q[7]), .in2(register_3_q[7]), .in3(register_4_q[7]),
    .out(multiplexer_1_out[7]), .sel(in_1), .en(in_2));
endmodule
