// Logisim project REGISTER TRANSFER(MEMORY).circ as structural Verilog: 1 circuit, main circuit main
module main (
  input  WRITE_READ,
  input  [1:0] in_2,
  input  [1:0] in_3,
  input  [1:0] in_4
);

  wire clock_1_out, decoder_1_out0, decoder_1_out1, decoder_1_out2, decoder_1_out3, not_1_out;
  wire [7:0] multiplexer_1_out, multiplexer_2_out, ram_1_data, register_1_q, register_2_q, register_3_q,
       register_4_q, register_5_q, register_6_q, register_7_q, register_8_q;

  Register register_1 (.Q(register_1_q), .clk(clock_1_out));  // open: D, en, clr
  Register register_2 (.Q(register_2_q), .clk(clock_1_out));  // open: D, en, clr
  Register register_3 (.Q(register_3_q), .clk(clock_1_out));  // open: D, en, clr
  Register register_4 (.Q(register_4_q), .clk(clock_1_out));  // open: D, en, clr
  Decoder #(.select(2)) decoder_1 (
    .out0(decoder_1_out0), .out1(decoder_1_out1), .out2(decoder_1_out2), .out3(decoder_1_out3), .sel(in_3));  // open: en
  Multiplexer #(.select(2), .width(8)) multiplexer_1 (
    .in0(register_1_q), .in1(register_2_q), .in2(register_3_q), .in3(register_4_q), .out(multiplexer_1_out),
    .sel(in_2));  // open: en
  Register register_5 (.D(ram_1_data), .en(decoder_1_out0), .Q(register_5_q), .clk(clock_1_out));  // open: clr
  Register register_6 (.D(ram_1_data), .en(decoder_1_out1), .Q(register_6_q), .clk(clock_1_out));  // open: clr
  Register register_7 (.D(ram_1_data), .en(decoder_1_out2), .Q(register_7_q), .clk(clock_1_out));  // open: clr
  Register register_8 (.D(ram_1_data), .en(decoder_1_out3), .Q(register_8_q), .clk(clock_1_out));  // open: clr
  not not_1 (not_1_out, WRITE_READ);
  RAM #(.bus("separate")) ram_1 (
    .addr(multiplexer_1_out), .din(multiplexer_2_out), .data(ram_1_data), .str(not_1_out), .clk(clock_1_out),
    .ld(WRITE_READ));  // open: sel, clr
  Multiplexer #(.select(2), .width(8)) multiplexer_2 (
    .in0(register_5_q), .in1(register_6_q), .in2(register_7_q), .in3(register_8_q), .out(multiplexer_2_out),
    .sel(in_4));  // open: en
  Clock clock_1 (.out(clock_1_out));
endmodule
