// Logisim project SIMPLE COMPUTER.circ as structural Verilog: 3 circuits, main circuit main
module main (
  input  in_1,
  input  RESET
);

  wire and_1_out, clock_1_out, combinational_circuit_1_x1, combinational_circuit_1_x2,
       combinational_circuit_1_x3, combinational_circuit_1_x4, combinational_circuit_1_x5,
       combinational_circuit_1_x6, combinational_circuit_1_x7, combinational_circuit_1_x8, decoder_1_out1,
       decoder_1_out2, decoder_1_out3, decoder_2_out0, decoder_2_out1, decoder_2_out2, decoder_2_out3,
       decoder_2_out4, decoder_2_out5, decoder_2_out6, decoder_2_out7, or_1_out, or_2_out, or_3_out;
  wire [1:0] IR_q;
  wire [2:0] counter_1_q;
  wire [7:0] MAR_q, MBR_q, mux_1_out_5, mux_2_out_5, PC_q, R_q, rom_1_data;
  wire [7:2] IR_q_2;

  Clock clock_1 (.out(clock_1_out));
  Counter PC (.count(combinational_circuit_1_x2), .Q(PC_q), .clk(clock_1_out), .clr(RESET));  // open: load, D, carry
  MUX mux_1 (.A1(MBR_q), .A2(PC_q), .S(combinational_circuit_1_x1), .E(in_1), .out_5(mux_1_out_5));
  Register IR (.D(MBR_q), .en(combinational_circuit_1_x4), .Q({IR_q_2, IR_q}), .clk(clock_1_out), .clr(RESET));
  Decoder #(.select(2)) decoder_1 (
    .out1(decoder_1_out1), .out2(decoder_1_out2), .out3(decoder_1_out3), .sel(IR_q), .en(in_1));  // open: out0
  Decoder #(.select(3)) decoder_2 (
    .out0(decoder_2_out0), .out1(decoder_2_out1), .out2(decoder_2_out2), .out3(decoder_2_out3),
    .out4(decoder_2_out4), .out5(decoder_2_out5), .out6(decoder_2_out6), .out7(decoder_2_out7),
    .sel(counter_1_q), .en(in_1));
  Combinational_Circuit combinational_circuit_1 (
    .q1(decoder_1_out1), .q2(decoder_1_out2), .q3(decoder_1_out3), .t0(decoder_2_out0), .t1(decoder_2_out1),
    .t2(decoder_2_out2), .t3(decoder_2_out3), .t4(decoder_2_out4), .t5(decoder_2_out5), .t6(decoder_2_out6),
    .t7(decoder_2_out7), .x1(combinational_circuit_1_x1), .x2(combinational_circuit_1_x2),
    .x3(combinational_circuit_1_x3), .x4(combinational_circuit_1_x4), .x5(combinational_circuit_1_x5),
    .x6(combinational_circuit_1_x6), .x7(combinational_circuit_1_x7), .x8(combinational_circuit_1_x8));
  Counter #(.width(3), .max('h7)) counter_1 (
    .Q(counter_1_q), .clk(clock_1_out), .clr(or_1_out));  // open: load, D, count, carry
  and and_1 (and_1_out, combinational_circuit_1_x7, clock_1_out);
  or or_1 (or_1_out, and_1_out, RESET);
  or or_2 (or_2_out, combinational_circuit_1_x1, combinational_circuit_1_x8);
  MUX mux_2 (.A1(MBR_q), .A2(R_q), .S(combinational_circuit_1_x5), .E(in_1), .out_5(mux_2_out_5));
  or or_3 (or_3_out, combinational_circuit_1_x5, combinational_circuit_1_x6);
  Register MAR (.D(mux_1_out_5), .en(or_2_out), .Q(MAR_q), .clk(clock_1_out), .clr(RESET));
  Register MBR (.D(rom_1_data), .en(combinational_circuit_1_x3), .Q(MBR_q), .clk(clock_1_out), .clr(RESET));
  Register R (.en(in_1), .Q(R_q), .clk(clock_1_out));  // open: D, clr
  Register A (.D(mux_2_out_5), .en(or_3_out), .clk(clock_1_out), .clr(RESET));  // open: Q
  ROM rom_1 (.addr(MAR_q), .data(rom_1_data), .sel(combinational_circuit_1_x3));

  // Notes on the sheet:
  //   contents of rom_1 (hex, n*v repeats v):
  //   1 2 9 3 8 0 0 0 27
endmodule

module Combinational_Circuit (
  input  q1,
  input  q2,
  input  q3,
  input  t0,
  input  t1,
  input  t2,
  input  t3,
  input  t4,
  input  t5,
  input  t6,
  input  t7,
  output x1,
  output x2,
  output x3,
  output x4,
  output x5,
  output x6,
  output x7,
  output x8
);

  wire and_1_out, and_2_out, and_3_out, and_5_out, and_6_out, or_1_out;

  or or_1 (or_1_out, q2, q3);
  and and_1 (and_1_out, or_1_out, t3);
  and and_2 (and_2_out, or_1_out, t4);
  and and_3 (and_3_out, q3, t6);
  and and_4 (x5, q1, t3);
  and and_5 (and_5_out, q2, t5);
  and and_6 (and_6_out, q3, t7);
  and and_7 (x8, q3, t5);
  or or_2 (x6, and_5_out, and_6_out);
  or or_3 (x1, t0, and_1_out);
  or or_4 (x2, and_2_out, t1);
  or or_5 (x3, x2, and_3_out);
  or or_6 (x7, x6, x5);

  assign x4 = t2;
endmodule

module MUX (
  input  [7:0] A1,
  input  [7:0] A2,
  input  S,
  input  E,
  output [7:0] out_5
);

  Multiplexer multiplexer_1 (.in0(A1[0]), .in1(A2[0]), .out(out_5[0]), .sel(S), .en(E));
  Multiplexer multiplexer_2 (.in0(A1[1]), .in1(A2[1]), .out(out_5[1]), .sel(S), .en(E));
  Multiplexer multiplexer_3 (.in0(A1[2]), .in1(A2[2]), .out(out_5[2]), .sel(S), .en(E));
  Multiplexer multiplexer_4 (.in0(A1[3]), .in1(A2[3]), .out(out_5[3]), .sel(S), .en(E));
  Multiplexer multiplexer_5 (.in0(A1[4]), .in1(A2[4]), .out(out_5[4]), .sel(S), .en(E));
  Multiplexer multiplexer_6 (.in0(A1[5]), .in1(A2[5]), .out(out_5[5]), .sel(S), .en(E));
  Multiplexer multiplexer_7 (.in0(A1[6]), .in1(A2[6]), .out(out_5[6]), .sel(S), .en(E));
  Multiplexer multiplexer_8 (.in0(A1[7]), .in1(A2[7]), .out(out_5[7]), .sel(S), .en(E));
endmodule
